# Fritzing sketch relay_uart1 (saved by Fritzing 0.9.3b)

parts:
  Arduino_Nano = Arduino Nano (Rev3.0)
  1ch_Relay = KY-019 5V Relay Module [package="Breakout board"]
  220V_Power_Socket = Lilypad Battery Connect
  220V_Power_Plug = Power plug

nets:
  N1: Arduino_Nano.GND, 1ch_Relay.-
  N2: Arduino_Nano.D7, 1ch_Relay.S
  N3: Arduino_Nano.5V, 1ch_Relay.+
  N4: 1ch_Relay.Common, 220V_Power_Socket.+
  N5: 1ch_Relay.NO, 220V_Power_Plug.VCC
  N6: 220V_Power_Socket.-, 220V_Power_Plug.GND

notes:
  220V Power Plug
  220V Wall Socket

custom parts:
  KY-019 5V Relay Module: KY-019 5V Relay module, used to control AC circuits. (Special thanks to vanepp for fixing the PCB holes and other errors)
